# Fritzing sketch sketch (saved by Fritzing 1.0.1rc)
circuit board: 8.46667cm x 5.64444cm
breadboards: 1

parts:
  DFRobot_DFPlayer_Mini1 = DFRobot DFPlayer Mini [part_number=DFR0299]
  A1 = Esp32-c3 super mini
  S1 = Round Pushbutton
  SP1 = SPEAKER [package=pcb_mount_speaker]

nets:
  N1: DFRobot_DFPlayer_Mini1.VCC, A1.Pin_16
  N2: DFRobot_DFPlayer_Mini1.RX, A1.Pin_8
  N3: DFRobot_DFPlayer_Mini1.TX, A1.Pin_7
  N4: DFRobot_DFPlayer_Mini1.SPK_1, SP1.-
  N5: DFRobot_DFPlayer_Mini1.GND-1, DFRobot_DFPlayer_Mini1.GND-2, A1.Pin_15, S1.leg1
  N6: DFRobot_DFPlayer_Mini1.SPK_2, SP1.+
  N7: DFRobot_DFPlayer_Mini1.BUSY, A1.Pin_6
  N8: A1.Pin_13, S1.leg0

notes:
  der button ist die Wählscheibe
  der Lautsprecher des Telefonhörers

custom parts:
  Esp32-c3 super mini: ESP32-C3 Development Board ESP32 SuperMini Development Board ESP32 Development Board WiFi Bluetooth.
